# Fritzing sketch esquema (saved by Fritzing 0.9.4)
breadboards: 1

parts:
  Componente1 = Photon
  RHT1 = Humidity and Temperature Sensor RHT03
  R1 = Resistor [tolerance=±5% resistance=10k package=THT]

nets:
  N1: Componente1.GND, RHT1.GND_2
  N2: Componente1.D2, RHT1.Data-signal, R1.Pin_0
  3V3: Componente1.3V3, RHT1.Vcc, R1.Pin_1
